// Logisim project Zhuang_Yufan.circ as structural Verilog: 8 circuits, main circuit main
module main (
);

  wire Clear, Clock, Clrst, ex_mem_buffer_1_lw, ex_mem_buffer_1_sel, idrr_ex_buffer_1_seloff, isE, isM,
       JClear, mem_wb_buffer_1_sel, mem_wb_buffer_1_wren, not_1_out, not_2_out, or_1_out, SelXY, Stall, SWX,
       TB;
  wire [1:0] idrr_ex_buffer_1_func;
  wire [3:0] blackbox_1_rx_2, ERx, ex_mem_buffer_1_opcode_2, idrr_ex_buffer_1_opcode_2,
       if_idrr_buffer_1_opcode, if_idrr_buffer_1_rx, mem_wb_buffer_1_rx_2, MRx, P1, P2, Ry, Rz;
  wire [19:0] if_idrr_buffer_1_offset;
  wire [23:0] PC_q;
  wire [31:0] adder_1_out, adder_2_out, bit_extender_1_out, blackbox_1_ryf, blackbox_1_rzf, blackbox_1_vrx,
       controlled_buffer_1_out, dual_ported_register_file_1_out1, dual_ported_register_file_1_out2, EFB,
       ex_mem_buffer_1_vrx_2, idrr_ex_buffer_1_pc_2, idrr_ex_buffer_1_vry_2, idrr_ex_buffer_1_vrz_2,
       if_idrr_buffer_1_pc_2, Jalr, mem_wb_buffer_1_valu_2, mem_wb_buffer_1_vmem_2, MFB, MFB0, MFB1,
       multiplexer_1_out, multiplexer_4_out, multiplexer_5_out, multiplexer_7_out, OffsetD, ram_1_data, vRx;
  wire [31:24] PC_q_2;

  Register #(.width(32)) PC (.D(multiplexer_4_out), .en(Clock), .Q({PC_q_2, PC_q}), .clk(Clock), .clr(Clear));
  not not_1 (not_1_out, or_1_out);
  or or_1 (or_1_out, TB, Stall);
  Adder #(.width(32)) adder_1 (.a(32'h1), .b({PC_q_2, PC_q}), .out(adder_1_out));  // open: cin, cout
  RAM #(.addrWidth(24), .dataWidth(32)) ram_1 (
    .addr(PC_q), .data(ram_1_data), .sel(not_1_out), .clk(Clock));  // open: ld, clr
  Multiplexer #(.width(32), .enable("false")) multiplexer_1 (
    .in0(ram_1_data), .in1({32{1'b0}}), .out(multiplexer_1_out), .sel(Stall));
  IF_IDRR_Buffer if_idrr_buffer_1 (
    .InstructIn(multiplexer_1_out), .OPcode(if_idrr_buffer_1_opcode), .Rx(if_idrr_buffer_1_rx), .Ry(Ry),
    .RZ(Rz), .offset(if_idrr_buffer_1_offset), .PC(adder_1_out), .PC_2(if_idrr_buffer_1_pc_2), .Clock(Clock),
    .Clear(JClear), .SeXY(SelXY), .SWX(SWX));
  Clock clock_1 (.out(Clock));
  Button button_1 (.out(Clear));
  Multiplexer #(.width(4), .enable("false")) multiplexer_2 (.in0(Ry), .in1(if_idrr_buffer_1_rx), .out(P1), .sel(SelXY));
  Multiplexer #(.width(4), .enable("false")) multiplexer_3 (.in0(Rz), .in1(Ry), .out(P2), .sel(SelXY));
  Multiplexer #(.select(2), .width(32), .enable("false")) multiplexer_4 (
    .in0(adder_1_out), .in1({PC_q_2, PC_q}), .in2(Jalr), .in3(Jalr), .out(multiplexer_4_out),
    .sel({TB, Stall}));
  // Probe on EFB
  Dual_Ported_Register_File dual_ported_register_file_1 (
    .CLK(Clock), .WrREGNO(mem_wb_buffer_1_rx_2), .RdREGNO1(P1), .RdREGNO2(P2), .INPUT(multiplexer_7_out),
    .OUT1(dual_ported_register_file_1_out1), .OUT2(dual_ported_register_file_1_out2),
    .WrEN(mem_wb_buffer_1_wren), .Clear(Clear));
  assign bit_extender_1_out = {{12{if_idrr_buffer_1_offset[19]}}, if_idrr_buffer_1_offset};  // Bit_Extender bit_extender_1
  // Probe on MFB
  BlackBox blackbox_1 (
    .OPcode(if_idrr_buffer_1_opcode), .vRy(dual_ported_register_file_1_out1), .MFB(MFB),
    .vRz(dual_ported_register_file_1_out2), .P1(P1), .P2(P2), .ERx(ERx), .MRx(MRx), .RyF(blackbox_1_ryf),
    .RzF(blackbox_1_rzf), .Stall(Stall), .ClearStall(Clrst), .Clear(JClear), .isE(isE), .isM(isM), .EFB(EFB),
    .Rx(if_idrr_buffer_1_rx), .Rx_2(blackbox_1_rx_2), .vRx(blackbox_1_vrx));
  assign controlled_buffer_1_out = SelXY ? dual_ported_register_file_1_out1 : 32'bz;  // Controlled_Buffer controlled_buffer_1
  IDRR_EX_Buffer idrr_ex_buffer_1 (
    .OPcode(if_idrr_buffer_1_opcode), .Rx(blackbox_1_rx_2), .VRz(blackbox_1_rzf),
    .OPcode_2(idrr_ex_buffer_1_opcode_2), .Rx_2(ERx), .VRy_2(idrr_ex_buffer_1_vry_2),
    .VRz_2(idrr_ex_buffer_1_vrz_2), .PC(if_idrr_buffer_1_pc_2), .PC_2(idrr_ex_buffer_1_pc_2),
    .Offset(bit_extender_1_out), .Offset_2(OffsetD), .SelOff(idrr_ex_buffer_1_seloff),
    .func(idrr_ex_buffer_1_func), .Clock(Clock), .Clear(JClear), .vRx_2(vRx), .VRy(blackbox_1_ryf),
    .isE(isE), .vRx(blackbox_1_vrx));
  Multiplexer #(.width(32), .enable("false")) multiplexer_5 (
    .in0(idrr_ex_buffer_1_vrz_2), .in1(OffsetD), .out(multiplexer_5_out), .sel(idrr_ex_buffer_1_seloff));
  Adder #(.width(32)) adder_2 (.a(idrr_ex_buffer_1_pc_2), .b(OffsetD), .out(adder_2_out));  // open: cin, cout
  ALU alu_1 (.FUNC(idrr_ex_buffer_1_func), .A(idrr_ex_buffer_1_vry_2), .B(multiplexer_5_out), .OUT(EFB));
  EX_MEM_Buffer ex_mem_buffer_1 (
    .OPcode(idrr_ex_buffer_1_opcode_2), .Rx(ERx), .ALUvalue(EFB), .OPcode_2(ex_mem_buffer_1_opcode_2),
    .Rx_2(MRx), .ALUvalue_2(MFB0), .vRx(vRx), .vRx_2(ex_mem_buffer_1_vrx_2), .LW(ex_mem_buffer_1_lw),
    .Sel(ex_mem_buffer_1_sel), .Offset(adder_2_out), .Offset_2(Jalr), .Clock(Clock), .Clear(JClear),
    .takebranch(TB), .isM(isM));
  Multiplexer #(.width(32), .enable("false")) multiplexer_6 (.in0(MFB0), .in1(MFB1), .out(MFB), .sel(isM));
  not not_2 (not_2_out, ex_mem_buffer_1_lw);
  RAM #(.addrWidth(24), .dataWidth(32), .bus("separate")) ram_2 (
    .addr(MFB0[23:0]), .din(ex_mem_buffer_1_vrx_2), .data(MFB1), .str(not_2_out), .sel(ex_mem_buffer_1_sel),
    .clk(Clock), .ld(ex_mem_buffer_1_lw));  // open: clr
  MEM_WB_Buffer mem_wb_buffer_1 (
    .Rx(MRx), .vALU(MFB0), .vMEM(MFB1), .Rx_2(mem_wb_buffer_1_rx_2), .vALU_2(mem_wb_buffer_1_valu_2),
    .vMEM_2(mem_wb_buffer_1_vmem_2), .Sel(mem_wb_buffer_1_sel), .WrEn(mem_wb_buffer_1_wren), .Clock(Clock),
    .Opcode(ex_mem_buffer_1_opcode_2), .JClear(JClear), .ClarS(Clrst));
  Multiplexer #(.width(32), .enable("false")) multiplexer_7 (
    .in0(mem_wb_buffer_1_valu_2), .in1(mem_wb_buffer_1_vmem_2), .out(multiplexer_7_out),
    .sel(mem_wb_buffer_1_sel));
endmodule

module Dual_Ported_Register_File (
  input  CLK,
  input  Clear,
  input  WrEN,
  input  [3:0] WrREGNO,
  input  [3:0] RdREGNO1,
  input  [3:0] RdREGNO2,
  input  [31:0] INPUT,
  output [31:0] OUT1,
  output [31:0] OUT2
);

  wire En_a0, En_a1, En_a2, En_a3, En_a4, En_at, En_fp, En_k0, En_ra, En_s0, En_s1, En_s2, En_s3, En_sp,
       En_v0;
  wire [31:0] a0, a1, a2, a3, a4, at, fp, k0, ra, s0, s1, s2, s3, sp, v0, zero;

  Decoder #(.select(4), .disabled(0)) decoder_1 (
    .out1(En_at), .out2(En_v0), .out3(En_a0), .out4(En_a1), .out5(En_a2), .out6(En_a3), .out7(En_a4),
    .out8(En_s0), .out9(En_s1), .out10(En_s2), .out11(En_s3), .out12(En_k0), .out13(En_sp), .out14(En_fp),
    .out15(En_ra), .sel(WrREGNO), .en(WrEN));  // open: out0
  Register #(.width(32), .trigger("high")) u_zero (.D(INPUT), .en(1'b0), .Q(zero), .clk(CLK), .clr(Clear));
  Register #(.width(32)) u_at (.D(INPUT), .en(En_at), .Q(at), .clk(CLK), .clr(Clear));
  Register #(.width(32)) u_v0 (.D(INPUT), .en(En_v0), .Q(v0), .clk(CLK), .clr(Clear));
  Register #(.width(32)) u_a0 (.D(INPUT), .en(En_a0), .Q(a0), .clk(CLK), .clr(Clear));
  Register #(.width(32)) u_a1 (.D(INPUT), .en(En_a1), .Q(a1), .clk(CLK), .clr(Clear));
  Register #(.width(32)) u_a2 (.D(INPUT), .en(En_a2), .Q(a2), .clk(CLK), .clr(Clear));
  Register #(.width(32)) u_a3 (.D(INPUT), .en(En_a3), .Q(a3), .clk(CLK), .clr(Clear));
  Register #(.width(32)) u_a4 (.D(INPUT), .en(En_a4), .Q(a4), .clk(CLK), .clr(Clear));
  Multiplexer #(.select(4), .width(32), .disabled(0), .enable("false")) multiplexer_1 (
    .in0(zero), .in1(at), .in2(v0), .in3(a0), .in4(a1), .in5(a2), .in6(a3), .in7(a4), .in8(s0), .in9(s1),
    .in10(s2), .in11(s3), .in12(k0), .in13(sp), .in14(fp), .in15(ra), .out(OUT2), .sel(RdREGNO2));
  Register #(.width(32)) u_s0 (.D(INPUT), .en(En_s0), .Q(s0), .clk(CLK), .clr(Clear));
  Register #(.width(32)) u_s1 (.D(INPUT), .en(En_s1), .Q(s1), .clk(CLK), .clr(Clear));
  Register #(.width(32)) u_s2 (.D(INPUT), .en(En_s2), .Q(s2), .clk(CLK), .clr(Clear));
  Register #(.width(32)) u_s3 (.D(INPUT), .en(En_s3), .Q(s3), .clk(CLK), .clr(Clear));
  Register #(.width(32)) u_k0 (.D(INPUT), .en(En_k0), .Q(k0), .clk(CLK), .clr(Clear));
  Register #(.width(32)) u_sp (.D(INPUT), .en(En_sp), .Q(sp), .clk(CLK), .clr(Clear));
  Register #(.width(32)) u_fp (.D(INPUT), .en(En_fp), .Q(fp), .clk(CLK), .clr(Clear));
  Register #(.width(32)) u_ra (.D(INPUT), .en(En_ra), .Q(ra), .clk(CLK), .clr(Clear));
  Multiplexer #(.select(4), .width(32), .disabled(0), .enable("false")) multiplexer_2 (
    .in0(zero), .in1(at), .in2(v0), .in3(a0), .in4(a1), .in5(a2), .in6(a3), .in7(a4), .in8(s0), .in9(s1),
    .in10(s2), .in11(s3), .in12(k0), .in13(sp), .in14(fp), .in15(ra), .out(OUT1), .sel(RdREGNO1));

  // Notes on the sheet:
  //   DO NOT MODIFY THIS FILE
endmodule

// FBUF
module IF_IDRR_Buffer (
  input  [31:0] PC,
  input  [31:0] InstructIn,
  input  Clear,
  input  Clock,
  output [31:0] PC_2,
  output [3:0] OPcode,
  output [3:0] Rx,
  output [3:0] Ry,
  output [3:0] RZ,
  output [19:0] offset,
  output SeXY,
  output SWX
);

  Register #(.width(32)) register_1 (.D(PC), .en(Clock), .Q(PC_2), .clk(Clock), .clr(Clear));
  Register #(.width(32)) register_2 (
    .D(InstructIn), .en(Clock), .Q({OPcode, Rx, Ry, offset}), .clk(Clock), .clr(Clear));
  ROM #(.addrWidth(4), .dataWidth(2)) rom_1 (.addr(OPcode), .data({SWX, SeXY}));  // open: sel

  assign RZ = offset[3:0];

  // Notes on the sheet:
  //   contents of rom_1 (hex, n*v repeats v):
  //   4*0 3 1 1
endmodule

// DBUF
module IDRR_EX_Buffer (
  input  [31:0] PC,
  input  Clock,
  input  Clear,
  input  [3:0] OPcode,
  input  [3:0] Rx,
  input  [31:0] VRy,
  input  [31:0] VRz,
  input  [31:0] Offset,
  input  [31:0] vRx,
  output [31:0] PC_2,
  output [3:0] OPcode_2,
  output SelOff,
  output [1:0] func,
  output isE,
  output [3:0] Rx_2,
  output [31:0] VRy_2,
  output [31:0] VRz_2,
  output [31:0] Offset_2,
  output [31:0] vRx_2
);

  Register #(.width(32)) register_1 (.D(PC), .en(Clock), .Q(PC_2), .clk(Clock), .clr(Clear));
  Register #(.width(4)) register_2 (.D(OPcode), .en(Clock), .Q(OPcode_2), .clk(Clock), .clr(Clear));
  Register #(.width(32)) register_3 (.D(VRy), .en(Clock), .Q(VRy_2), .clk(Clock), .clr(Clear));
  Register #(.width(32)) register_4 (.D(VRz), .en(Clock), .Q(VRz_2), .clk(Clock), .clr(Clear));
  Register #(.width(4)) register_5 (.D(Rx), .en(Clock), .Q(Rx_2), .clk(Clock), .clr(Clear));
  Register #(.width(32)) register_6 (.D(Offset), .en(Clock), .Q(Offset_2), .clk(Clock), .clr(Clear));
  Register #(.width(32)) register_7 (.D(vRx), .en(Clock), .Q(vRx_2), .clk(Clock), .clr(Clear));
  ROM #(.addrWidth(4), .dataWidth(4)) rom_1 (.addr(OPcode_2), .data({isE, func, SelOff}));  // open: sel

  // Notes on the sheet:
  //   contents of rom_1 (hex, n*v repeats v):
  //   8 a 9 9 1 4 8
endmodule

// EBUF
module EX_MEM_Buffer (
  input  [3:0] OPcode,
  input  Clock,
  input  Clear,
  input  [31:0] Offset,
  input  [3:0] Rx,
  input  [31:0] ALUvalue,
  input  [31:0] vRx,
  output [3:0] OPcode_2,
  output LW,
  output Sel,
  output isM,
  output [31:0] Offset_2,
  output [31:0] ALUvalue_2,
  output [3:0] Rx_2,
  output takebranch,
  output [31:0] vRx_2
);

  wire and_1_out, BJ, comparator_1_eq, isJ, tovRx;
  wire [31:0] register_2_q, register_4_q;

  Register #(.width(4)) register_1 (.D(OPcode), .en(Clock), .Q(OPcode_2), .clk(Clock), .clr(Clear));
  Register #(.width(32)) register_2 (.D(Offset), .en(Clock), .Q(register_2_q), .clk(Clock), .clr(Clear));
  Register #(.width(4)) register_3 (.D(Rx), .en(Clock), .Q(Rx_2), .clk(Clock), .clr(Clear));
  Register #(.width(32)) register_4 (.D(ALUvalue), .en(Clock), .Q(register_4_q), .clk(Clock), .clr(Clear));
  Register #(.width(32)) register_5 (.D(vRx), .en(Clock), .Q(vRx_2), .clk(Clock), .clr(Clear));
  Comparator #(.width(32)) comparator_1 (.a(register_4_q), .b({32{1'b0}}), .eq(comparator_1_eq));  // open: gt, lt
  ROM #(.addrWidth(4), .dataWidth(5)) rom_1 (.addr(OPcode_2), .data({isM, tovRx, BJ, Sel, LW}));  // open: sel
  ROM #(.addrWidth(4), .dataWidth(1)) rom_2 (.addr(OPcode_2), .data(isJ));  // open: sel
  Multiplexer #(.width(32), .enable("false")) multiplexer_1 (
    .in0(register_4_q), .in1(register_2_q), .out(ALUvalue_2), .sel(isJ));
  Multiplexer #(.width(32), .enable("false")) multiplexer_2 (
    .in0(register_2_q), .in1(vRx_2), .out(Offset_2), .sel(tovRx));
  and and_1 (and_1_out, BJ, comparator_1_eq);
  or or_1 (takebranch, tovRx, and_1_out);

  // Notes on the sheet:
  //   contents of rom_1 (hex, n*v repeats v):
  //   0 0 0 13 2 4 c
  //   contents of rom_2 (hex, n*v repeats v):
  //   6*0 1
endmodule

// MBUF
module MEM_WB_Buffer (
  input  [3:0] Opcode,
  input  Clock,
  input  [3:0] Rx,
  input  [31:0] vALU,
  input  [31:0] vMEM,
  output Sel,
  output WrEn,
  output JClear,
  output ClarS,
  output [3:0] Rx_2,
  output [31:0] vALU_2,
  output [31:0] vMEM_2
);

  wire [3:0] register_1_q;

  Register #(.width(4)) register_1 (.D(Opcode), .en(Clock), .Q(register_1_q), .clk(Clock), .clr(JClear));
  Register #(.width(4)) register_2 (.D(Rx), .en(Clock), .Q(Rx_2), .clk(Clock), .clr(JClear));
  Register #(.width(32)) register_3 (.D(vALU), .en(Clock), .Q(vALU_2), .clk(Clock), .clr(JClear));
  Register #(.width(32)) register_4 (.D(vMEM), .en(Clock), .Q(vMEM_2), .clk(Clock), .clr(JClear));
  ROM #(.addrWidth(4), .dataWidth(4)) rom_1 (.addr(register_1_q), .data({ClarS, JClear, WrEn, Sel}));  // open: sel

  // Notes on the sheet:
  //   contents of rom_1 (hex, n*v repeats v):
  //   2 2 2 b 0 8 e
endmodule

module ALU (
  input  [1:0] FUNC,
  input  [31:0] A,
  input  [31:0] B,
  output [31:0] OUT
);

  wire [31:0] adder_1_out, adder_2_out, nand_1_out, subtractor_1_out;

  Adder #(.width(32)) adder_1 (.a(A), .b(B), .out(adder_1_out), .cin(1'b0));  // open: cout
  assign nand_1_out = ~(A & B);  // NAND_Gate nand_1, 32 bits wide
  Subtractor #(.width(32)) subtractor_1 (.a(A), .b(B), .out(subtractor_1_out), .bin(1'b0));  // open: bout
  Adder #(.width(32)) adder_2 (.a(A), .b(B), .out(adder_2_out), .cin(1'b1));  // open: cout
  Multiplexer #(.select(2), .width(32), .disabled(0), .enable("false")) multiplexer_1 (
    .in0(adder_1_out), .in1(nand_1_out), .in2(subtractor_1_out), .in3(adder_2_out), .out(OUT), .sel(FUNC));

  // Notes on the sheet:
  //   DO NOT MODIFY THIS
endmodule

module BlackBox (
  input  isE,
  input  isM,
  input  [3:0] OPcode,
  input  ClearStall,
  input  Clear,
  input  [31:0] vRy,
  input  [31:0] EFB,
  input  [31:0] MFB,
  input  [3:0] P1,
  input  [3:0] Rx,
  input  [31:0] vRz,
  input  [3:0] P2,
  input  [3:0] ERx,
  input  [3:0] MRx,
  output Stall,
  output [31:0] RyF,
  output [31:0] vRx,
  output [3:0] Rx_2,
  output [31:0] RzF
);

  wire and_3_out, ChangeX, comparator_1_eq, comparator_2_eq, comparator_3_eq, comparator_4_eq,
       comparator_5_eq, comparator_6_eq, comparator_7_eq, EorM, forwardY, forwardZ, fromE, fromM,
       multiplexer_5_out, multiplexer_6_out, not_1_out, not_2_out, not_3_out, not_4_out, or_1_out, or_2_out,
       or_3_out, or_5_out, or_6_out, or_7_out, rom_2_data, Stall0, StallBJ;
  wire [31:0] demultiplexer_1_out0, multiplexer_1_out, multiplexer_2_out;

  Multiplexer #(.width(32), .enable("false")) multiplexer_1 (.in0(EFB), .in1(MFB), .out(multiplexer_1_out), .sel(EorM));
  ROM #(.addrWidth(4), .dataWidth(2)) rom_1 (.addr(OPcode), .data({ChangeX, StallBJ}));  // open: sel
  ROM #(.addrWidth(4), .dataWidth(1)) rom_2 (.addr(OPcode), .data(rom_2_data));  // open: sel
  Comparator #(.width(4)) comparator_1 (.a(P1), .b(ERx), .eq(comparator_1_eq));  // open: gt, lt
  Comparator #(.width(4)) comparator_2 (.a(ERx), .b(P2), .eq(comparator_2_eq));  // open: gt, lt
  Comparator #(.width(4)) comparator_3 (.a(P1), .b(MRx), .eq(comparator_3_eq));  // open: gt, lt
  Comparator #(.width(4)) comparator_4 (.a(MRx), .b(P2), .eq(comparator_4_eq));  // open: gt, lt
  Multiplexer #(.width(32), .enable("false")) multiplexer_2 (
    .in0(vRy), .in1(multiplexer_1_out), .out(multiplexer_2_out), .sel(forwardY));
  Comparator #(.width(4)) comparator_5 (.a(MRx), .b(4'b0000), .eq(comparator_5_eq));  // open: gt, lt
  or or_1 (or_1_out, StallBJ, Stall0);
  Register #(.width(1)) register_1 (.D(or_1_out), .en(or_1_out), .Q(Stall), .clk(or_1_out), .clr(or_2_out));
  or or_2 (or_2_out, ClearStall, Clear);
  Demultiplexer #(.width(32), .enable("false")) demultiplexer_1 (
    .out0(demultiplexer_1_out0), .out1(vRx), .in(multiplexer_2_out), .sel(rom_2_data));
  Multiplexer #(.width(32), .enable("false")) multiplexer_3 (
    .in0(vRz), .in1(multiplexer_1_out), .out(RzF), .sel(forwardZ));
  or or_3 (or_3_out, comparator_3_eq, comparator_4_eq);
  or or_4 (fromE, comparator_1_eq, comparator_2_eq);
  or or_5 (or_5_out, comparator_3_eq, comparator_4_eq);
  not not_1 (not_1_out, comparator_5_eq);
  Multiplexer #(.enable("false")) multiplexer_4 (.in0(1'b0), .in1(or_3_out), .out(Stall0), .sel(isM));
  and and_1 (fromM, or_5_out, not_1_out);
  Multiplexer #(.enable("false")) multiplexer_5 (
    .in0(comparator_1_eq), .in1(comparator_3_eq), .out(multiplexer_5_out), .sel(EorM));
  Multiplexer #(.enable("false")) multiplexer_6 (
    .in0(comparator_2_eq), .in1(comparator_4_eq), .out(multiplexer_6_out), .sel(EorM));
  Multiplexer #(.width(32), .enable("false")) multiplexer_7 (
    .in0(demultiplexer_1_out0), .in1(RzF), .out(RyF), .sel(rom_2_data));
  not not_2 (not_2_out, comparator_7_eq);
  or or_6 (or_6_out, multiplexer_5_out, comparator_3_eq);
  Comparator #(.width(4)) comparator_6 (.a(ERx), .b(4'b0000), .eq(comparator_6_eq));  // open: gt, lt
  Comparator #(.width(4)) comparator_7 (.a(ERx), .b(4'b0000), .eq(comparator_7_eq));  // open: gt, lt
  and and_2 (forwardY, not_2_out, or_6_out);
  not not_3 (not_3_out, comparator_6_eq);
  and and_3 (and_3_out, fromE, isE);
  or or_7 (or_7_out, isM, fromM);
  Multiplexer #(.width(4), .enable("false")) multiplexer_8 (.in0(Rx), .in1(P2), .out(Rx_2), .sel(ChangeX));
  and and_4 (forwardZ, not_3_out, multiplexer_6_out);
  not not_4 (not_4_out, and_3_out);
  and and_5 (EorM, not_4_out, or_7_out);

  // Notes on the sheet:
  //   contents of rom_1 (hex, n*v repeats v):
  //   5*0 1 3
  //   contents of rom_2 (hex, n*v repeats v):
  //   4*0 1 0 1
endmodule
